// Logisim project datapath.circ as structural Verilog: 4 circuits, main circuit Datapath
module Datapath (
  input  Reset,
  input  Clear,
  input  Clear_2
);

  wire alu_1_p4, and_1_out, Clock_out, control_1_branch, control_1_escrevemem, control_1_escrevereg,
       control_1_jump, control_1_lemem, control_1_memparareg, control_1_origalu, control_1_regdst,
       instructiondecode_1_p1, instructiondecode_1_p3, instructiondecode_1_p7, jumpaddress_1_p1, not_1_out,
       registerfile_1_p2, wordaddress_1_p2, wordaddress_2_p2;
  wire [1:0] control_1_opalu;
  wire [3:0] alucontrol_1_operation;
  wire [4:0] instructiondecode_1_p4, instructiondecode_1_p5, multiplexer_1_out;
  wire [5:0] instructiondecode_1_p2, instructiondecode_1_p6;
  wire [31:0] branchaddress_1_p3, jumpaddress_1_p2, jumpaddress_1_p3, mips_ram_2_p4, multiplexer_2_out,
       multiplexer_3_out, multiplexer_5_out, register_1_q, registerfile_1_p1, registerfile_1_p3,
       signextend_1_p6, wordaddress_2_p1;

  Register #(.width(32)) register_1 (
    .D(multiplexer_5_out), .Q(register_1_q), .clk(Clock_out), .clr(Reset));  // open: en
  Clock Clock (.out(Clock_out));
  // WordAddress wordaddress_1: pin names not known; wires that end beside it: register_1_q, wordaddress_1_p2, wordaddress_1_p2, 1'b0, 4'b1111
  // JumpAddress jumpaddress_1: pin names not known; wires that end beside it: jumpaddress_1_p1, jumpaddress_1_p2, jumpaddress_1_p3
  // InstructionDecode instructiondecode_1: pin names not known; wires that end beside it: instructiondecode_1_p1, instructiondecode_1_p2, instructiondecode_1_p3, instructiondecode_1_p4, instructiondecode_1_p5, instructiondecode_1_p6, instructiondecode_1_p7, jumpaddress_1_p1
  // MIPS_RAM mips_ram_1: pin names not known; wires that end beside it: 1'b0, 1'b1, Clear, instructiondecode_1_p1
  Control control_1 (
    .op(instructiondecode_1_p2), .RegDst(control_1_regdst), .Branch(control_1_branch),
    .LeMem(control_1_lemem), .MemparaReg(control_1_memparareg), .OpALU(control_1_opalu),
    .EscreveMem(control_1_escrevemem), .OrigALU(control_1_origalu), .EscreveReg(control_1_escrevereg),
    .Jump(control_1_jump));
  Multiplexer #(.width(5), .enable("false")) multiplexer_1 (
    .in0(instructiondecode_1_p4), .in1(instructiondecode_1_p5), .out(multiplexer_1_out),
    .sel(control_1_regdst));
  Adder #(.width(32)) adder_1 (.a(32'h4), .b(register_1_q), .out(jumpaddress_1_p2));  // open: cin, cout
  not not_1 (not_1_out, Clock_out);
  // SignExtend signextend_1: pin names not known; wires that end beside it: not_1_out, control_1_escrevereg, multiplexer_1_out, instructiondecode_1_p7, instructiondecode_1_p3, signextend_1_p6, instructiondecode_1_p4
  // RegisterFile registerfile_1: pin names not known; wires that end beside it: registerfile_1_p1, registerfile_1_p2, registerfile_1_p3
  Multiplexer #(.width(32), .enable("false")) multiplexer_2 (
    .in0(registerfile_1_p3), .in1(signextend_1_p6), .out(multiplexer_2_out), .sel(control_1_origalu));
  // WordAddress wordaddress_2: pin names not known; wires that end beside it: wordaddress_2_p1, wordaddress_2_p2, wordaddress_2_p2, registerfile_1_p3, control_1_escrevemem, 4'b1111
  ALUcontrol alucontrol_1 (.funct(instructiondecode_1_p6), .OpALU(control_1_opalu), .Operation(alucontrol_1_operation));
  // BranchAddress branchaddress_1: pin names not known; wires that end beside it: jumpaddress_1_p2, signextend_1_p6, branchaddress_1_p3
  and and_1 (and_1_out, control_1_branch, alu_1_p4);
  // ALU alu_1: pin names not known; wires that end beside it: registerfile_1_p2, multiplexer_2_out, alucontrol_1_operation, alu_1_p4, wordaddress_2_p1
  // MIPS_RAM mips_ram_2: pin names not known; wires that end beside it: Clock_out, control_1_lemem, Clear_2, mips_ram_2_p4
  Multiplexer #(.width(32), .enable("false")) multiplexer_3 (
    .in0(jumpaddress_1_p2), .in1(branchaddress_1_p3), .out(multiplexer_3_out), .sel(and_1_out));
  Multiplexer #(.width(32), .enable("false")) multiplexer_4 (
    .in0(wordaddress_2_p1), .in1(mips_ram_2_p4), .out(registerfile_1_p1), .sel(control_1_memparareg));
  Multiplexer #(.width(32), .enable("false")) multiplexer_5 (
    .in0(multiplexer_3_out), .in1(jumpaddress_1_p3), .out(multiplexer_5_out), .sel(control_1_jump));

  // Notes on the sheet:
  //   PC
  //   Opcode
  //   8c0a0000
  //   8c0b0004
  //   014b4820
  //   ac090008
  //   1000ffff
  //   Memória de Instruções
  //   Instruções
  //   Decodificador
  //   main:  lw $t2, 0($zero) 
  //   lw $t3, 4($zero)
  //   add $t1, $t2, $t3
  //   sw $t1, 8($zero)
  //   exit:  beq $zero, $zero, exit
  //   Controle
  //   Controle
  //   lw    001100011
  //   lw    001100011
  //   R     100010001
  //   sw    X00X00110
  //   beq   X10X01000
  //   Registradores
  //   Extensão
  //   Controle ALU
  //   0010 add
  //   0010 add
  //   0010 add
  //   0010 add
  //   0110 sub
  //   ALU
  //   Memória de Dados
  //   Branch
endmodule

module Control (
  input  [5:0] op,
  output RegDst,
  output Branch,
  output LeMem,
  output MemparaReg,
  output [1:0] OpALU,
  output EscreveMem,
  output OrigALU,
  output EscreveReg,
  output Jump
);

  wire and_6_out, not_1_out, not_2_out, not_3_out, not_4_out, not_5_out, not_6_out, not_7_out, not_8_out,
       not_9_out, not_10_out, not_11_out, not_12_out, not_13_out, not_14_out, not_15_out, not_16_out,
       not_17_out, not_18_out, not_19_out, not_20_out, not_21_out, not_22_out, not_23_out, not_24_out,
       not_25_out, not_26_out;

  not not_1 (not_1_out, op[5]);
  not not_2 (not_2_out, op[4]);
  not not_3 (not_3_out, op[3]);
  not not_4 (not_4_out, op[1]);
  not not_5 (not_5_out, op[0]);
  not not_6 (not_6_out, op[2]);
  not not_7 (not_7_out, op[4]);
  and and_1 (OpALU[1], not_1_out, not_2_out, not_3_out, not_6_out, not_4_out, not_5_out);
  not not_8 (not_8_out, op[2]);
  not not_9 (not_9_out, op[4]);
  not not_10 (not_10_out, op[3]);
  and and_2 (LeMem, op[5], not_7_out, not_10_out, not_8_out, op[1], op[0]);
  not not_11 (not_11_out, op[4]);
  not not_12 (not_12_out, op[2]);
  not not_13 (not_13_out, op[5]);
  and and_3 (EscreveMem, op[5], not_9_out, op[3], not_12_out, op[1], op[0]);
  not not_14 (not_14_out, op[3]);
  not not_15 (not_15_out, op[5]);
  not not_16 (not_16_out, op[4]);
  not not_17 (not_17_out, op[0]);
  not not_18 (not_18_out, op[1]);
  and and_4 (Branch, not_13_out, not_11_out, not_14_out, op[2], not_18_out, not_17_out);
  not not_19 (not_19_out, op[5]);
  not not_20 (not_20_out, op[3]);
  not not_21 (not_21_out, op[4]);
  not not_22 (not_22_out, op[0]);
  not not_23 (not_23_out, op[2]);
  and and_5 (Jump, not_15_out, not_16_out, not_20_out, not_23_out, op[1], not_22_out);
  or or_1 (OrigALU, LeMem, EscreveMem, and_6_out);
  or or_2 (EscreveReg, OpALU[1], LeMem, and_6_out);
  not not_24 (not_24_out, op[2]);
  not not_25 (not_25_out, op[0]);
  not not_26 (not_26_out, op[1]);
  and and_6 (and_6_out, not_19_out, not_21_out, op[3], not_24_out, not_26_out, not_25_out);

  assign MemparaReg = LeMem;
  assign OpALU[0] = Branch;
  assign RegDst = OpALU[1];

  // Notes on the sheet:
  //   R-Format
  //   lw
  //   sw
  //   beq
  //   jump
  //   addi
endmodule

module ALUcontrol (
  input  [1:0] OpALU,
  input  [5:0] funct,
  output [3:0] Operation
);

  wire and_1_out, not_1_out, not_2_out, not_3_out, or_1_out;

  or or_1 (or_1_out, funct[3], funct[0]);
  and and_1 (and_1_out, OpALU[1], funct[1]);
  and and_2 (Operation[0], OpALU[1], or_1_out);
  and and_3 (Operation[3], OpALU[0], not_1_out);
  not not_1 (not_1_out, OpALU[0]);
  or or_2 (Operation[2], OpALU[0], and_1_out);
  not not_2 (not_2_out, OpALU[1]);
  or or_3 (Operation[1], not_2_out, not_3_out);
  not not_3 (not_3_out, funct[2]);
endmodule

module jAddress (
  input  [25:0] address,
  input  [31:0] jumpAddress,
  input  [31:0] PC
);


  assign {jumpAddress[27:2], jumpAddress[0]} = {address, jumpAddress[1]};
  assign PC[31:28] = jumpAddress[31:28];
  // also tied to GND on the sheet: jumpAddress[1]
endmodule
