// Logisim project somador.circ as structural Verilog: 2 circuits, main circuit main
module main (
  input  C0,
  input  A3,
  input  B3,
  input  A2,
  input  B2,
  input  A1,
  input  B1,
  input  A0,
  input  B0,
  output S0,
  output S0_2,
  output S1,
  output S0_3
);

  wire S0_cout, S1_cout, S2_cout;

  somador S3 (.cin(S2_cout), .a(A3), .b(B3), .s(S0));  // open: cout
  somador S2 (.cin(S1_cout), .a(A2), .b(B2), .s(S0_2), .cout(S2_cout));
  somador u_S1 (.cin(S0_cout), .a(A1), .b(B1), .s(S1), .cout(S1_cout));
  somador u_S0 (.cin(C0), .a(A0), .b(B0), .s(S0_3), .cout(S0_cout));
endmodule

// S
module somador (
  input  cin,
  input  a,
  input  b,
  output s,
  output cout
);

  wire A2_out, A3_out, A4_out, X1_out;

  xor X1 (X1_out, a, b);
  and A2 (A2_out, a, b);
  and A3 (A3_out, a, cin);
  and A4 (A4_out, b, cin);
  xor X2 (s, X1_out, cin);
  or O1 (cout, A2_out, A3_out, A4_out);
endmodule
