// Logisim project somador_sub_c2.circ as structural Verilog: 2 circuits, main circuit main
module main (
  input  C0,
  input  A3,
  input  B3,
  input  A2,
  input  B2,
  input  A1,
  input  B1,
  input  A0,
  input  B0,
  output OVERFLOW,
  output S0,
  output S0_2,
  output S1,
  output S0_3
);

  wire S0_cout, S1_cout, S2_cout, S3_cout, xor_2_out, xor_3_out, xor_4_out, xor_5_out;

  xor xor_1 (OVERFLOW, S2_cout, S3_cout);
  somador S3 (.cin(S2_cout), .a(A3), .b(xor_2_out), .s(S0), .cout(S3_cout));
  xor xor_2 (xor_2_out, B3, C0);
  xor xor_3 (xor_3_out, B2, C0);
  somador S2 (.cin(S1_cout), .a(A2), .b(xor_3_out), .s(S0_2), .cout(S2_cout));
  xor xor_4 (xor_4_out, B1, C0);
  somador u_S1 (.cin(S0_cout), .a(A1), .b(xor_4_out), .s(S1), .cout(S1_cout));
  somador u_S0 (.cin(C0), .a(A0), .b(xor_5_out), .s(S0_3), .cout(S0_cout));
  xor xor_5 (xor_5_out, B0, C0);
endmodule

// S
module somador (
  input  cin,
  input  a,
  input  b,
  output s,
  output cout
);

  wire A2_out, A3_out, A4_out, X1_out;

  xor X1 (X1_out, a, b);
  and A2 (A2_out, a, b);
  and A3 (A3_out, a, cin);
  and A4 (A4_out, b, cin);
  xor X2 (s, X1_out, cin);
  or O1 (cout, A2_out, A3_out, A4_out);
endmodule
