// Logisim project somador_sub_c2_mux.circ as structural Verilog: 3 circuits, main circuit main
module main (
  input  A3,
  input  B3,
  input  A2,
  input  B2,
  input  A1,
  input  B1,
  input  A0,
  input  B0,
  input  C0,
  output OVERFLOW,
  output S0,
  output S0_2,
  output S1,
  output S0_3
);

  wire mux_2x1_1_s, mux_2x1_2_s, mux_2x1_3_s, mux_2x1_4_s, not_1_out, not_2_out, not_3_out, not_4_out,
       S0_cout, S1_cout, S2_cout, S3_cout;

  xor xor_1 (OVERFLOW, S2_cout, S3_cout);
  mux_2x1 mux_2x1_1 (.E0(B3), .E1(not_1_out), .S(mux_2x1_1_s), .C(C0));
  somador S3 (.cin(S2_cout), .a(A3), .b(mux_2x1_1_s), .s(S0), .cout(S3_cout));
  not not_1 (not_1_out, B3);
  not not_2 (not_2_out, B2);
  mux_2x1 mux_2x1_2 (.E0(B2), .E1(not_2_out), .S(mux_2x1_2_s), .C(C0));
  somador S2 (.cin(S1_cout), .a(A2), .b(mux_2x1_2_s), .s(S0_2), .cout(S2_cout));
  not not_3 (not_3_out, B1);
  mux_2x1 mux_2x1_3 (.E0(B1), .E1(not_3_out), .S(mux_2x1_3_s), .C(C0));
  somador u_S1 (.cin(S0_cout), .a(A1), .b(mux_2x1_3_s), .s(S1), .cout(S1_cout));
  somador u_S0 (.cin(C0), .a(A0), .b(mux_2x1_4_s), .s(S0_3), .cout(S0_cout));
  not not_4 (not_4_out, B0);
  mux_2x1 mux_2x1_4 (.E0(B0), .E1(not_4_out), .S(mux_2x1_4_s), .C(C0));
endmodule

// S
module somador (
  input  cin,
  input  a,
  input  b,
  output s,
  output cout
);

  wire A2_out, A3_out, A4_out, X1_out;

  xor X1 (X1_out, a, b);
  and A2 (A2_out, a, b);
  and A3 (A3_out, a, cin);
  and A4 (A4_out, b, cin);
  xor X2 (s, X1_out, cin);
  or O1 (cout, A2_out, A3_out, A4_out);

  // Notes on the sheet:
  //   xor2
  //   and3
  //   and3
  //   and3
  //   s_X1_X2
  //   s_A2_O1
  //   s_A3_O1
  //   s_A4_O1
  //   xor2
  //   s_X2_A1
  //   or3
  //   and2
endmodule

// M
module mux_2x1 (
  input  C,
  input  E0,
  input  E1,
  output S
);

  wire and_1_out, and_2_out, not_1_out;

  not not_1 (not_1_out, C);
  and and_1 (and_1_out, not_1_out, E0);
  and and_2 (and_2_out, C, E1);
  or or_1 (S, and_1_out, and_2_out);
endmodule
